# Fritzing sketch kop_munka (saved by Fritzing 0.9.3b)
breadboards: 1

parts:
  Part1 = Arduino Mega 2560 (Rev3)
  KY-1 = Keyes Relay [package=THT]
  M1 = DC Motor
  DHT11_1 = DHT11 module
  Part2 = LCD1602-I2C
  LCD2004-I2C1 = LCD2004-I2C
  DS1 = DS18B20 1-Wire Temperature Sensor Probe Cable
  Part4 = KY-018 Photoresistor Module [package="Breakout board"]
  Part6 = FC-28 Soil Hygrometer Module
  부품2 = FC-28 Soil Hygrometer Module - Probe
  S1 = Momentary Switch [package=ksa_sealed_tac_switch]
  S2 = Momentary Switch [package=ksa_sealed_tac_switch]
  S3 = Momentary Switch [package=ksa_sealed_tac_switch]
  Part7 = KY-016 RGB Full Color LED Module [package="Breakout board"]
  Part8 = KY-012 Active Buzzer Module [package="Breakout board"]

nets:
  N1: Part1.A4, Part4.S
  N2: Part1.A5, Part6.AO
  N3: Part1.D21/SCL, Part1.SCL, Part2.SCL, LCD2004-I2C1.SCL
  N4: Part1.D20/SDA, Part1.SDA, Part2.SDA, LCD2004-I2C1.SDA
  N5: Part1.D12_PWM, DHT11_1.DATA
  N6: Part1.D11_PWM, DS1.shield
  N7: Part1.D10_PWM, KY-1.signal
  N8: Part1.D9_PWM, S3.2
  N9: Part1.D8_PWM, S1.2
  GND: Part1.GND, KY-1.ground, M1.pin_2, DHT11_1.GND, Part2.GND, LCD2004-I2C1.GND, DS1.GND, Part4.-, Part6.GND, S2.4, S3.4, Part7.-, Part8.-
  N10: Part1.D6_PWM, Part8.S
  N11: Part1.D7_PWM, S2.2
  VCC: Part1.5V, KY-1.power, KY-1.C, DHT11_1.VCC, Part2.VCC, LCD2004-I2C1.VCC, DS1.VDD, Part4.Vin, Part6.VCC
  N12: Part1.D53, Part7.R
  N13: KY-1.NO, M1.pin_1
  N14: Part6.POS, 부품2.POS
  N15: Part6.NEG, 부품2.NEG

custom parts:
  Keyes Relay: The Keyes 5V relay module is suitable for SCM development, home appliance control. It uses a 5V~12V TIL control signal which can control DC / AC signal.
  DHT11 module: DHT11 black pcb module
  LCD1602-I2C: A standard character display, usually with 2x16 characters. Comes in many colors with LCM1602 IIC attached.
  LCD2004-I2C: A standard character display with 4x20 characters. Comes in many colors with LCM2004 IIC attached.
  KY-018 Photoresistor Module: KY-018 Photoresistor module, used to measure light intensity. It can determine the presence or absence of light.
  FC-28 Soil Hygrometer Module: The FC-28 is a soil hygrometer module that uses the Texas Instruments LM393 comparator chip to provide an analog measurement of soil humidity. The digital output is high when soil moisture is over a certain threshold, as determined by adjusting the potentiometer.
  FC-28 Soil Hygrometer Module - Probe: The FC-28 is a soil hygrometer module that uses the Texas Instruments LM393 comparator chip to provide an analog measurement of soil humidity.
  KY-016 RGB Full Color LED Module: KY-016 Arduino full color 5mm RGB LED, different colors can be obtained by mixing the three primary colors.
  KY-012 Active Buzzer Module: Active Piezoelectric Buzzer Module Keyes KY-012, it produces single-tone sound when signal is high.
